// Logisim project Processor.circ as structural Verilog: 36 circuits, main circuit main
module main (
  input  SET_FGI,
  input  SET_FGO,
  input  Start,
  input  [7:0] in_4,
  output out_5,
  output [11:0] out_6,
  output out_7,
  output out_8,
  output [11:0] out_9,
  output out_10,
  output out_11,
  output [15:0] out_12,
  output out_13,
  output out_14,
  output [15:0] out_15,
  output [7:0] out_16,
  output [15:0] out_17,
  output [15:0] out_18,
  output [7:0] out_19
);

  wire AC_allbitsor, AC_bit15, arithmeticlogicunit16bit_1_cout, CLK_out, controlled_buffer_1_out,
       controlunit_1_ac_clr, controlunit_1_ac_inc, controlunit_1_ac_ld, controlunit_1_alu_b,
       controlunit_1_alu_cin, controlunit_1_alu_s0, controlunit_1_alu_s1, controlunit_1_alu_s2,
       controlunit_1_alu_s3, controlunit_1_ar_clr, controlunit_1_ar_inc, controlunit_1_ar_ld,
       controlunit_1_counterr, controlunit_1_dr_inc, controlunit_1_dr_ld, controlunit_1_e_toggle,
       controlunit_1_fgi_r, controlunit_1_fgo_r, controlunit_1_ien_toggle, controlunit_1_ir_ld,
       controlunit_1_m_rd, controlunit_1_m_wrt, controlunit_1_outr_ld, controlunit_1_pc_clr,
       controlunit_1_pc_inc, controlunit_1_pc_ld, controlunit_1_r_toggle, controlunit_1_s_r,
       controlunit_1_tr_ld, DR_allbitsor, not_1_out;
  wire [2:0] controlunit_1_commonbus;
  wire [3:0] SC_o;
  wire [6:0] decoder4bit_1_t0;
  wire [7:0] bit_extender_3_out, decoder3bit_1_d0;
  wire [11:0] bit_extender_1_out, bit_extender_2_out;
  wire [15:0] arithmeticlogicunit16bit_1_f, bit_extender_4_out, bit_extender_5_out, bit_extender_6_out,
       Memory_dout, multiplexer_1_out, multiplexer_2_out;

  D_Flip_Flop I (.D(out_17[15]), .clk(CLK_out), .Q(out_5));  // open: Qn, preset, reset
  T_Flip_Flop R (.T(controlunit_1_r_toggle), .clk(CLK_out), .Q(out_7));  // open: Qn, reset, preset
  T_Flip_Flop IEN (.T(controlunit_1_ien_toggle), .clk(CLK_out), .Q(out_8));  // open: Qn, reset, preset
  D_Flip_Flop FGI (.D(SET_FGI), .clk(CLK_out), .Q(out_10), .reset(controlunit_1_fgi_r));  // open: Qn, preset
  D_Flip_Flop FGO (.D(SET_FGO), .clk(CLK_out), .Q(out_11), .reset(controlunit_1_fgo_r));  // open: Qn, preset
  D_Flip_Flop S (.D(Start), .clk(CLK_out), .Q(out_13), .reset(controlunit_1_s_r));  // open: Qn, preset
  T_Flip_Flop E (.T(controlunit_1_e_toggle), .clk(CLK_out), .Q(out_14));  // open: Qn, reset, preset
  Decoder3Bit decoder3bit_1 (
    .I(out_17[14:12]), .E(1'b1), .D0(decoder3bit_1_d0[0]), .D1(decoder3bit_1_d0[1]),
    .D2(decoder3bit_1_d0[2]), .D3(decoder3bit_1_d0[3]), .D4(decoder3bit_1_d0[4]), .D5(decoder3bit_1_d0[5]),
    .D6(decoder3bit_1_d0[6]), .D7(decoder3bit_1_d0[7]));
  Decoder4Bit decoder4bit_1 (
    .I(SC_o), .T0(decoder4bit_1_t0[0]), .T1(decoder4bit_1_t0[1]), .T2(decoder4bit_1_t0[2]),
    .T3(decoder4bit_1_t0[3]), .T4(decoder4bit_1_t0[4]), .T5(decoder4bit_1_t0[5]), .T6(decoder4bit_1_t0[6]));  // open: T7, T8, T9, T10, B11, T12, T13, T14, T15
  Counter4Bit SC (.R(controlunit_1_counterr), .CLK(controlled_buffer_1_out), .O(SC_o));  // open: I, H, L
  ControlUnit controlunit_1 (
    .I(out_5), .R(out_7), .IEN(out_8), .FGI(out_10), .FGO(out_11), .S(out_13), .E(out_14),
    .T0(decoder4bit_1_t0[0]), .T1(decoder4bit_1_t0[1]), .T2(decoder4bit_1_t0[2]), .T3(decoder4bit_1_t0[3]),
    .T4(decoder4bit_1_t0[4]), .T5(decoder4bit_1_t0[5]), .T6(decoder4bit_1_t0[6]), .D0(decoder3bit_1_d0[0]),
    .D1(decoder3bit_1_d0[1]), .D2(decoder3bit_1_d0[2]), .D3(decoder3bit_1_d0[3]), .D4(decoder3bit_1_d0[4]),
    .D5(decoder3bit_1_d0[5]), .D6(decoder3bit_1_d0[6]), .D7(decoder3bit_1_d0[7]), .B0(out_17[0]),
    .B1(out_17[1]), .B2(out_17[2]), .B3(out_17[3]), .B4(out_17[4]), .B5(out_17[5]), .B6(out_17[6]),
    .B7(out_17[7]), .B8(out_17[8]), .B9(out_17[9]), .B10(out_17[10]), .B11(out_17[11]), .DR(DR_allbitsor),
    .AC15(AC_bit15), .AC(AC_allbitsor), .COUT(arithmeticlogicunit16bit_1_cout), .M_WRT(controlunit_1_m_wrt),
    .M_RD(controlunit_1_m_rd), .AR_LD(controlunit_1_ar_ld), .AR_CLR(controlunit_1_ar_clr),
    .AR_INC(controlunit_1_ar_inc), .PC_LD(controlunit_1_pc_ld), .PC_CLR(controlunit_1_pc_clr),
    .PC_INC(controlunit_1_pc_inc), .DR_LD(controlunit_1_dr_ld), .DR_INC(controlunit_1_dr_inc),
    .AC_LD(controlunit_1_ac_ld), .AC_CLR(controlunit_1_ac_clr), .AC_INC(controlunit_1_ac_inc),
    .ALU_CIN(controlunit_1_alu_cin), .ALU_S0(controlunit_1_alu_s0), .ALU_S1(controlunit_1_alu_s1),
    .ALU_S2(controlunit_1_alu_s2), .ALU_S3(controlunit_1_alu_s3), .ALU_B(controlunit_1_alu_b),
    .IR_LD(controlunit_1_ir_ld), .TR_LD(controlunit_1_tr_ld), .OUTR_LD(controlunit_1_outr_ld),
    .CommonBus(controlunit_1_commonbus), .CounterR(controlunit_1_counterr),
    .R_TOGGLE(controlunit_1_r_toggle), .IEN_TOGGLE(controlunit_1_ien_toggle), .FGI_R(controlunit_1_fgi_r),
    .FGO_R(controlunit_1_fgo_r), .S_R(controlunit_1_s_r), .E_TOGGLE(controlunit_1_e_toggle));
  assign controlled_buffer_1_out = out_13 ? CLK_out : 1'bz;  // Controlled_Buffer controlled_buffer_1
  not not_1 (not_1_out, controlunit_1_m_rd);
  RAM #(.addrWidth(12), .asyncread("true"), .dataWidth(16)) Memory (
    .addr(out_6), .we(controlunit_1_m_wrt), .oe(not_1_out), .clk(CLK_out), .din(multiplexer_2_out),
    .dout(Memory_dout));
  Multiplexer #(.width(16)) multiplexer_1 (
    .in0(out_12), .in1(bit_extender_6_out), .out(multiplexer_1_out), .sel(controlunit_1_alu_b));
  ArithmeticLogicUnit16Bit arithmeticlogicunit16bit_1 (
    .S3(controlunit_1_alu_s3), .S2(controlunit_1_alu_s2), .S1(controlunit_1_alu_s1),
    .S0(controlunit_1_alu_s0), .A(out_15), .B(multiplexer_1_out), .CIN(controlunit_1_alu_cin),
    .COUT(arithmeticlogicunit16bit_1_cout), .F(arithmeticlogicunit16bit_1_f));
  Clock CLK (.out(CLK_out));
  Bit_Extender #(.in_width(16), .out_width(12)) bit_extender_1 (.in(multiplexer_2_out), .out(bit_extender_1_out));
  Bit_Extender #(.in_width(16), .out_width(12)) bit_extender_2 (.in(multiplexer_2_out), .out(bit_extender_2_out));
  Bit_Extender #(.in_width(16), .out_width(8)) bit_extender_3 (.in(multiplexer_2_out), .out(bit_extender_3_out));
  Register12Bit AR (
    .I(bit_extender_1_out), .INC(controlunit_1_ar_inc), .LD(controlunit_1_ar_ld), .CLK(CLK_out),
    .R(controlunit_1_ar_clr), .O(out_6));
  Register12Bit PC (
    .I(bit_extender_2_out), .INC(controlunit_1_pc_inc), .LD(controlunit_1_pc_ld), .CLK(CLK_out),
    .R(controlunit_1_pc_clr), .O(out_9));
  Register16Bit DR (
    .I(multiplexer_2_out), .INC(controlunit_1_dr_inc), .LD(controlunit_1_dr_ld), .CLK(CLK_out),
    .AllBitsOR(DR_allbitsor), .O(out_12));  // open: R, Bit15
  Register16Bit AC (
    .I(arithmeticlogicunit16bit_1_f), .INC(controlunit_1_ac_inc), .LD(controlunit_1_ac_ld), .CLK(CLK_out),
    .R(controlunit_1_ac_clr), .AllBitsOR(AC_allbitsor), .O(out_15), .Bit15(AC_bit15));
  Register8Bit INPR (.I(in_4), .LD(1'b1), .CLK(CLK_out), .O(out_16));
  Register16Bit IR (
    .I(multiplexer_2_out), .LD(controlunit_1_ir_ld), .CLK(CLK_out), .O(out_17));  // open: INC, R, AllBitsOR, Bit15
  Register16Bit TR (
    .I(multiplexer_2_out), .LD(controlunit_1_tr_ld), .CLK(CLK_out), .O(out_18));  // open: INC, R, AllBitsOR, Bit15
  Register8Bit OUTR (.I(bit_extender_3_out), .LD(controlunit_1_outr_ld), .CLK(CLK_out), .O(out_19));
  assign bit_extender_4_out = {{4{out_6[11]}}, out_6};  // Bit_Extender bit_extender_4
  assign bit_extender_5_out = {{4{out_9[11]}}, out_9};  // Bit_Extender bit_extender_5
  assign bit_extender_6_out = {{8{out_16[7]}}, out_16};  // Bit_Extender bit_extender_6
  Multiplexer #(.select(3), .width(16)) multiplexer_2 (
    .in1(bit_extender_4_out), .in2(bit_extender_5_out), .in3(out_12), .in4(out_15), .in5(out_17),
    .in6(out_18), .in7(Memory_dout), .out(multiplexer_2_out), .sel(controlunit_1_commonbus));  // open: in0
endmodule

module Register8Bit (
  input  [7:0] I,
  input  LD,
  input  CLK,
  output [7:0] O
);

  wire [7:0] multiplexer_1_out;

  Multiplexer #(.width(8)) multiplexer_1 (.in0(O), .in1(I), .out(multiplexer_1_out), .sel(LD));
  D_Flip_Flop d_ff_1 (.D(multiplexer_1_out[0]), .clk(CLK), .Q(O[0]));  // open: Qn, preset, reset
  D_Flip_Flop d_ff_2 (.D(multiplexer_1_out[1]), .clk(CLK), .Q(O[1]));  // open: Qn, preset, reset
  D_Flip_Flop d_ff_3 (.D(multiplexer_1_out[2]), .clk(CLK), .Q(O[2]));  // open: Qn, preset, reset
  D_Flip_Flop d_ff_4 (.D(multiplexer_1_out[3]), .clk(CLK), .Q(O[3]));  // open: Qn, preset, reset
  D_Flip_Flop d_ff_5 (.D(multiplexer_1_out[4]), .clk(CLK), .Q(O[4]));  // open: Qn, preset, reset
  D_Flip_Flop d_ff_6 (.D(multiplexer_1_out[5]), .clk(CLK), .Q(O[5]));  // open: Qn, preset, reset
  D_Flip_Flop d_ff_7 (.D(multiplexer_1_out[6]), .clk(CLK), .Q(O[6]));  // open: Qn, preset, reset
  D_Flip_Flop d_ff_8 (.D(multiplexer_1_out[7]), .clk(CLK), .Q(O[7]));  // open: Qn, preset, reset
endmodule

module Decoder2Bit (
  input  [1:0] I,
  output B0,
  output B1,
  output B2,
  output B3
);

  wire not_1_out, not_2_out;

  not not_1 (not_1_out, I[1]);
  not not_2 (not_2_out, I[0]);
  and and_1 (B0, not_2_out, not_1_out);
  and and_2 (B1, I[0], not_1_out);
  and and_3 (B2, I[1], not_2_out);
  and and_4 (B3, I[0], I[1]);
endmodule

module Adder8Bit (
  input  [7:0] A,
  input  [7:0] B,
  input  SUB,
  output [7:0] R,
  output CarryOut
);

  wire [7:0] multiplexer_1_out, not_1_out;

  Multiplexer #(.width(8)) multiplexer_1 (.in0(B), .in1(not_1_out), .out(multiplexer_1_out), .sel(SUB));
  assign not_1_out = ~B;  // NOT_Gate not_1, 8 bits wide
  Adder adder_1 (.a(A), .b(multiplexer_1_out), .out(R), .cin(SUB), .cout(CarryOut));
endmodule

module Counter4Bit (
  input  [3:0] I,
  input  R,
  input  H,
  input  L,
  input  CLK,
  output [3:0] O
);

  wire and_1_out, and_2_out, not_1_out, not_2_out;
  wire [1:0] or_1_out;
  wire [3:0] fulladder4bit_1_s, multiplexer_1_out;

  not not_1 (not_1_out, R);
  not not_2 (not_2_out, H);
  and and_1 (and_1_out, not_1_out, H);
  and and_2 (and_2_out, not_1_out, not_2_out, L);
  or or_1 (or_1_out[0], and_1_out, R);
  or or_2 (or_1_out[1], and_2_out, R);
  Multiplexer #(.select(2), .width(4)) multiplexer_1 (
    .in0(fulladder4bit_1_s), .in1(O), .in2(I), .in3(4'b0000), .out(multiplexer_1_out), .sel(or_1_out));
  Register4Bit register4bit_1 (.I(multiplexer_1_out), .LD(1'b1), .CLK(CLK), .O(O));
  FullAdder4Bit fulladder4bit_1 (.A(O), .CIN(1'b1), .S(fulladder4bit_1_s));  // open: B, COUT
endmodule

module Decoder4Bit (
  input  [3:0] I,
  output T0,
  output T1,
  output T2,
  output T3,
  output T4,
  output T5,
  output T6,
  output T7,
  output T8,
  output T9,
  output T10,
  output B11,
  output T12,
  output T13,
  output T14,
  output T15
);

  wire not_1_out, not_2_out, not_3_out, not_4_out;

  not not_1 (not_1_out, I[3]);
  not not_2 (not_2_out, I[2]);
  not not_3 (not_3_out, I[1]);
  not not_4 (not_4_out, I[0]);
  and and_1 (T0, not_4_out, not_3_out, not_2_out, not_1_out);
  and and_2 (T1, I[0], not_3_out, not_2_out, not_1_out);
  and and_3 (T2, not_4_out, I[1], not_2_out, not_1_out);
  and and_4 (T3, I[0], I[1], not_2_out, not_1_out);
  and and_5 (T4, not_4_out, not_3_out, I[2], not_1_out);
  and and_6 (T5, I[0], not_3_out, I[2], not_1_out);
  and and_7 (T6, not_4_out, I[1], I[2], not_1_out);
  and and_8 (T7, I[0], I[1], I[2], not_1_out);
  and and_9 (T8, not_4_out, not_3_out, not_2_out, I[3]);
  and and_10 (T9, I[0], not_3_out, not_2_out, I[3]);
  and and_11 (T10, not_4_out, I[1], not_2_out, I[3]);
  and and_12 (B11, I[0], I[1], not_2_out, I[3]);
  and and_13 (T12, not_4_out, not_3_out, I[2], I[3]);
  and and_14 (T13, I[0], not_3_out, I[2], I[3]);
  and and_15 (T14, not_4_out, I[1], I[2], I[3]);
  and and_16 (T15, I[0], I[1], I[2], I[3]);
endmodule

module Register12Bit (
  input  [11:0] I,
  input  INC,
  input  LD,
  input  CLK,
  input  R,
  output [11:0] O
);

  wire [11:0] fulladder12bit_1_s, multiplexer_1_out, multiplexer_2_out;

  Multiplexer #(.width(12)) multiplexer_1 (.in0(multiplexer_2_out), .in1(I), .out(multiplexer_1_out), .sel(LD));
  D_Flip_Flop d_ff_1 (.D(multiplexer_1_out[0]), .clk(CLK), .Q(O[0]), .reset(R));  // open: Qn, preset
  D_Flip_Flop d_ff_2 (.D(multiplexer_1_out[1]), .clk(CLK), .Q(O[1]), .reset(R));  // open: Qn, preset
  D_Flip_Flop d_ff_3 (.D(multiplexer_1_out[2]), .clk(CLK), .Q(O[2]), .reset(R));  // open: Qn, preset
  D_Flip_Flop d_ff_4 (.D(multiplexer_1_out[3]), .clk(CLK), .Q(O[3]), .reset(R));  // open: Qn, preset
  D_Flip_Flop d_ff_5 (.D(multiplexer_1_out[4]), .clk(CLK), .Q(O[4]), .reset(R));  // open: Qn, preset
  D_Flip_Flop d_ff_6 (.D(multiplexer_1_out[5]), .clk(CLK), .Q(O[5]), .reset(R));  // open: Qn, preset
  D_Flip_Flop d_ff_7 (.D(multiplexer_1_out[6]), .clk(CLK), .Q(O[6]), .reset(R));  // open: Qn, preset
  D_Flip_Flop d_ff_8 (.D(multiplexer_1_out[7]), .clk(CLK), .Q(O[7]), .reset(R));  // open: Qn, preset
  D_Flip_Flop d_ff_9 (.D(multiplexer_1_out[8]), .clk(CLK), .Q(O[8]), .reset(R));  // open: Qn, preset
  D_Flip_Flop d_ff_10 (.D(multiplexer_1_out[9]), .clk(CLK), .Q(O[9]), .reset(R));  // open: Qn, preset
  D_Flip_Flop d_ff_11 (.D(multiplexer_1_out[10]), .clk(CLK), .Q(O[10]), .reset(R));  // open: Qn, preset
  D_Flip_Flop d_ff_12 (.D(multiplexer_1_out[11]), .clk(CLK), .Q(O[11]), .reset(R));  // open: Qn, preset
  Multiplexer #(.width(12)) multiplexer_2 (.in0(O), .in1(fulladder12bit_1_s), .out(multiplexer_2_out), .sel(INC));
  FullAdder12Bit fulladder12bit_1 (.A(O), .CIN(1'b1), .S(fulladder12bit_1_s));  // open: B, COUT
endmodule

module Register16Bit (
  input  [15:0] I,
  input  INC,
  input  LD,
  input  CLK,
  input  R,
  output AllBitsOR,
  output [15:0] O,
  output Bit15
);

  wire [15:0] fulladder16bit_1_s, multiplexer_1_out, multiplexer_2_out;

  Multiplexer #(.width(16)) multiplexer_1 (.in0(multiplexer_2_out), .in1(I), .out(multiplexer_1_out), .sel(LD));
  D_Flip_Flop d_ff_1 (.D(multiplexer_1_out[0]), .clk(CLK), .Q(O[0]), .reset(R));  // open: Qn, preset
  D_Flip_Flop d_ff_2 (.D(multiplexer_1_out[1]), .clk(CLK), .Q(O[1]), .reset(R));  // open: Qn, preset
  D_Flip_Flop d_ff_3 (.D(multiplexer_1_out[2]), .clk(CLK), .Q(O[2]), .reset(R));  // open: Qn, preset
  D_Flip_Flop d_ff_4 (.D(multiplexer_1_out[3]), .clk(CLK), .Q(O[3]), .reset(R));  // open: Qn, preset
  D_Flip_Flop d_ff_5 (.D(multiplexer_1_out[4]), .clk(CLK), .Q(O[4]), .reset(R));  // open: Qn, preset
  D_Flip_Flop d_ff_6 (.D(multiplexer_1_out[5]), .clk(CLK), .Q(O[5]), .reset(R));  // open: Qn, preset
  D_Flip_Flop d_ff_7 (.D(multiplexer_1_out[6]), .clk(CLK), .Q(O[6]), .reset(R));  // open: Qn, preset
  D_Flip_Flop d_ff_8 (.D(multiplexer_1_out[7]), .clk(CLK), .Q(O[7]), .reset(R));  // open: Qn, preset
  D_Flip_Flop d_ff_9 (.D(multiplexer_1_out[8]), .clk(CLK), .Q(O[8]), .reset(R));  // open: Qn, preset
  D_Flip_Flop d_ff_10 (.D(multiplexer_1_out[9]), .clk(CLK), .Q(O[9]), .reset(R));  // open: Qn, preset
  D_Flip_Flop d_ff_11 (.D(multiplexer_1_out[10]), .clk(CLK), .Q(O[10]), .reset(R));  // open: Qn, preset
  D_Flip_Flop d_ff_12 (.D(multiplexer_1_out[11]), .clk(CLK), .Q(O[11]), .reset(R));  // open: Qn, preset
  D_Flip_Flop d_ff_13 (.D(multiplexer_1_out[12]), .clk(CLK), .Q(O[12]), .reset(R));  // open: Qn, preset
  D_Flip_Flop d_ff_14 (.D(multiplexer_1_out[13]), .clk(CLK), .Q(O[13]), .reset(R));  // open: Qn, preset
  D_Flip_Flop d_ff_15 (.D(multiplexer_1_out[14]), .clk(CLK), .Q(O[14]), .reset(R));  // open: Qn, preset
  D_Flip_Flop d_ff_16 (.D(multiplexer_1_out[15]), .clk(CLK), .Q(Bit15), .reset(R));  // open: Qn, preset
  Multiplexer #(.width(16)) multiplexer_2 (
    .in0({Bit15, O[14:0]}), .in1(fulladder16bit_1_s), .out(multiplexer_2_out), .sel(INC));
  or or_1 (AllBitsOR, O[0], O[1], O[2], O[3], O[4], O[5], O[6], O[7], O[8], O[9], O[10], O[11], O[12], O[13], O[14], Bit15);
  FullAdder16Bit fulladder16bit_1 (.A({Bit15, O[14:0]}), .CIN(1'b1), .S(fulladder16bit_1_s));  // open: B, COUT

  assign O[15] = Bit15;
endmodule

module Decoder3Bit (
  input  [2:0] I,
  input  E,
  output D0,
  output D1,
  output D2,
  output D3,
  output D4,
  output D5,
  output D6,
  output D7
);

  wire not_1_out, not_2_out, not_3_out;
  wire [2:0] controlled_buffer_1_out;

  assign controlled_buffer_1_out = E ? I : 3'bz;  // Controlled_Buffer controlled_buffer_1
  not not_1 (not_1_out, controlled_buffer_1_out[2]);
  not not_2 (not_2_out, controlled_buffer_1_out[1]);
  not not_3 (not_3_out, controlled_buffer_1_out[0]);
  and and_1 (D0, not_3_out, not_2_out, not_1_out);
  and and_2 (D1, controlled_buffer_1_out[0], not_2_out, not_1_out);
  and and_3 (D2, not_3_out, controlled_buffer_1_out[1], not_1_out);
  and and_4 (D3, controlled_buffer_1_out[0], controlled_buffer_1_out[1], not_1_out);
  and and_5 (D4, not_3_out, not_2_out, controlled_buffer_1_out[2]);
  and and_6 (D5, controlled_buffer_1_out[0], not_2_out, controlled_buffer_1_out[2]);
  and and_7 (D6, not_3_out, controlled_buffer_1_out[1], controlled_buffer_1_out[2]);
  and and_8 (D7, controlled_buffer_1_out[0], controlled_buffer_1_out[1], controlled_buffer_1_out[2]);
endmodule

module ArithmeticUnit16Bit (
  input  [15:0] A,
  input  [15:0] B,
  input  CIN,
  input  S0,
  input  S1,
  output COUT,
  output [15:0] D
);

  wire [15:0] multiplexer_1_out, not_1_out;

  assign not_1_out = ~B;  // NOT_Gate not_1, 16 bits wide
  Multiplexer #(.select(2), .width(16)) multiplexer_1 (
    .in0(B), .in1(not_1_out), .in2({16{1'b0}}), .in3(16'h1), .out(multiplexer_1_out), .sel({S1, S0}));
  FullAdder16Bit fulladder16bit_1 (.A(A), .B(multiplexer_1_out), .CIN(CIN), .COUT(COUT), .S(D));
endmodule

module FullAdder16Bit (
  input  [15:0] A,
  input  [15:0] B,
  input  CIN,
  output COUT,
  output [15:0] S
);

  wire fulladder1bit_1_cout, fulladder1bit_2_cout, fulladder1bit_3_cout, fulladder1bit_4_cout,
       fulladder1bit_5_cout, fulladder1bit_6_cout, fulladder1bit_7_cout, fulladder1bit_8_cout,
       fulladder1bit_9_cout, fulladder1bit_10_cout, fulladder1bit_11_cout, fulladder1bit_12_cout,
       fulladder1bit_13_cout, fulladder1bit_14_cout, fulladder1bit_15_cout;

  FullAdder1Bit fulladder1bit_1 (.A(A[0]), .B(B[0]), .CIN(CIN), .S(S[0]), .COUT(fulladder1bit_1_cout));
  FullAdder1Bit fulladder1bit_2 (.A(A[1]), .B(B[1]), .CIN(fulladder1bit_1_cout), .S(S[1]), .COUT(fulladder1bit_2_cout));
  FullAdder1Bit fulladder1bit_3 (.A(A[2]), .B(B[2]), .CIN(fulladder1bit_2_cout), .S(S[2]), .COUT(fulladder1bit_3_cout));
  FullAdder1Bit fulladder1bit_4 (.A(A[3]), .B(B[3]), .CIN(fulladder1bit_3_cout), .S(S[3]), .COUT(fulladder1bit_4_cout));
  FullAdder1Bit fulladder1bit_5 (.A(A[4]), .B(B[4]), .CIN(fulladder1bit_4_cout), .S(S[4]), .COUT(fulladder1bit_5_cout));
  FullAdder1Bit fulladder1bit_6 (.A(A[5]), .B(B[5]), .CIN(fulladder1bit_5_cout), .S(S[5]), .COUT(fulladder1bit_6_cout));
  FullAdder1Bit fulladder1bit_7 (.A(A[6]), .B(B[6]), .CIN(fulladder1bit_6_cout), .S(S[6]), .COUT(fulladder1bit_7_cout));
  FullAdder1Bit fulladder1bit_8 (.A(A[7]), .B(B[7]), .CIN(fulladder1bit_7_cout), .S(S[7]), .COUT(fulladder1bit_8_cout));
  FullAdder1Bit fulladder1bit_9 (.A(A[8]), .B(B[8]), .CIN(fulladder1bit_8_cout), .S(S[8]), .COUT(fulladder1bit_9_cout));
  FullAdder1Bit fulladder1bit_10 (
    .A(A[9]), .B(B[9]), .CIN(fulladder1bit_9_cout), .S(S[9]), .COUT(fulladder1bit_10_cout));
  FullAdder1Bit fulladder1bit_11 (
    .A(A[10]), .B(B[10]), .CIN(fulladder1bit_10_cout), .S(S[10]), .COUT(fulladder1bit_11_cout));
  FullAdder1Bit fulladder1bit_12 (
    .A(A[11]), .B(B[11]), .CIN(fulladder1bit_11_cout), .S(S[11]), .COUT(fulladder1bit_12_cout));
  FullAdder1Bit fulladder1bit_13 (
    .A(A[12]), .B(B[12]), .CIN(fulladder1bit_12_cout), .S(S[12]), .COUT(fulladder1bit_13_cout));
  FullAdder1Bit fulladder1bit_14 (
    .A(A[13]), .B(B[13]), .CIN(fulladder1bit_13_cout), .S(S[13]), .COUT(fulladder1bit_14_cout));
  FullAdder1Bit fulladder1bit_15 (
    .A(A[14]), .B(B[14]), .CIN(fulladder1bit_14_cout), .S(S[14]), .COUT(fulladder1bit_15_cout));
  FullAdder1Bit fulladder1bit_16 (.A(A[15]), .B(B[15]), .CIN(fulladder1bit_15_cout), .S(S[15]), .COUT(COUT));
endmodule

module FullAdder1Bit (
  input  A,
  input  B,
  input  CIN,
  output S,
  output COUT
);

  wire and_1_out, and_2_out, xor_1_out;

  xor xor_1 (xor_1_out, A, B);
  and and_1 (and_1_out, A, B);
  and and_2 (and_2_out, CIN, xor_1_out);
  xor xor_2 (S, xor_1_out, CIN);
  or or_1 (COUT, and_2_out, and_1_out);
endmodule

module LogicUnit16Bit (
  input  [15:0] A,
  input  [15:0] B,
  input  S0,
  input  S1,
  input  CIN,
  output [15:0] E
);

  wire [15:0] and_1_out, and_2_out, and_3_out, not_1_out, or_1_out, or_2_out, or_3_out, xor_1_out;

  assign and_1_out = A & B;  // AND_Gate and_1, 16 bits wide
  assign or_1_out = A | B;  // OR_Gate or_1, 16 bits wide
  assign xor_1_out = A ^ B;  // XOR_Gate xor_1, 16 bits wide
  assign not_1_out = ~A;  // NOT_Gate not_1, 16 bits wide
  assign and_2_out = A & 16'hff00;  // AND_Gate and_2, 16 bits wide
  assign and_3_out = A & 16'hff;  // AND_Gate and_3, 16 bits wide
  assign or_2_out = and_2_out | B;  // OR_Gate or_2, 16 bits wide
  assign or_3_out = and_3_out | {B[7:0], B[15:8]};  // OR_Gate or_3, 16 bits wide
  Multiplexer #(.select(3), .width(16)) multiplexer_1 (
    .in0(and_1_out), .in1(or_1_out), .in2(xor_1_out), .in3(not_1_out), .in4(or_2_out), .in5(or_3_out),
    .in6(B), .in7({16{1'b1}}), .out(E), .sel({S1, S0, CIN}));
endmodule

module ArithmeticLogicUnit16Bit (
  input  S3,
  input  S2,
  input  S1,
  input  S0,
  input  [15:0] A,
  input  [15:0] B,
  input  CIN,
  output COUT,
  output [15:0] F
);

  wire arithmeticunit16bit_1_cout, shifterunit16bit_1_cout;
  wire [15:0] arithmeticunit16bit_1_d, logicunit16bit_1_e, shifterunit16bit_1_s;

  ArithmeticUnit16Bit arithmeticunit16bit_1 (
    .A(A), .B(B), .CIN(CIN), .S0(S0), .S1(S1), .COUT(arithmeticunit16bit_1_cout), .D(arithmeticunit16bit_1_d));
  LogicUnit16Bit logicunit16bit_1 (.A(A), .B(B), .S0(S0), .S1(S1), .CIN(CIN), .E(logicunit16bit_1_e));
  ShifterUnit16Bit shifterunit16bit_1 (
    .A(A), .CIN(CIN), .SR(S1), .RL(S0), .COUT(shifterunit16bit_1_cout), .S(shifterunit16bit_1_s));
  Multiplexer multiplexer_1 (.in0(arithmeticunit16bit_1_cout), .in1(shifterunit16bit_1_cout), .out(COUT), .sel(S3));
  Multiplexer #(.select(2), .width(16)) multiplexer_2 (
    .in0(arithmeticunit16bit_1_d), .in1(logicunit16bit_1_e), .in2(shifterunit16bit_1_s), .out(F),
    .sel({S3, S2}));  // open: in3
endmodule

module ShifterUnit16Bit (
  input  [15:0] A,
  input  CIN,
  input  SR,
  input  RL,
  output COUT,
  output [15:0] S
);

  Multiplexer multiplexer_1 (.in0(A[0]), .in1(A[15]), .out(COUT), .sel(RL));
  Multiplexer #(.select(2), .width(16)) multiplexer_2 (
    .in0({CIN, A[15:1]}), .in1({A[14:0], CIN}), .in2({CIN, A[15:1]}), .in3({A[14:0], CIN}), .out(S),
    .sel({SR, RL}));

  // Notes on the sheet:
  //   SHL
  //   SHR
  //   CIR
  //   CIL
endmodule

module ControlUnit (
  input  I,
  input  R,
  input  IEN,
  input  FGI,
  input  FGO,
  input  S,
  input  E,
  input  T0,
  input  T1,
  input  T2,
  input  T3,
  input  T4,
  input  T5,
  input  T6,
  input  D0,
  input  D1,
  input  D2,
  input  D3,
  input  D4,
  input  D5,
  input  D6,
  input  D7,
  input  B0,
  input  B1,
  input  B2,
  input  B3,
  input  B4,
  input  B5,
  input  B6,
  input  B7,
  input  B8,
  input  B9,
  input  B10,
  input  B11,
  input  DR,
  input  AC15,
  input  AC,
  input  COUT,
  output M_WRT,
  output M_RD,
  output AR_LD,
  output AR_CLR,
  output AR_INC,
  output PC_LD,
  output PC_CLR,
  output PC_INC,
  output DR_LD,
  output DR_INC,
  output AC_LD,
  output AC_CLR,
  output AC_INC,
  output ALU_CIN,
  output ALU_S0,
  output ALU_S1,
  output ALU_S2,
  output ALU_S3,
  output ALU_B,
  output IR_LD,
  output TR_LD,
  output OUTR_LD,
  output [2:0] CommonBus,
  output CounterR,
  output R_TOGGLE,
  output IEN_TOGGLE,
  output FGI_R,
  output FGO_R,
  output S_R,
  output E_TOGGLE
);

  ControlUnitMemory controlunitmemory_1 (
    .R(R), .I(I), .T1(T1), .T3(T3), .T4(T4), .T6(T6), .D0(D0), .D1(D1), .D2(D2), .D3(D3), .D5(D5), .D6(D6),
    .D7(D7), .M_WRT(M_WRT), .M_RD(M_RD));
  ControlUnitAR controlunitar_1 (
    .R(R), .I(I), .T0(T0), .T2(T2), .T3(T3), .T4(T4), .D5(D5), .D7(D7), .AR_LD(AR_LD), .AR_CLR(AR_CLR),
    .AR_INC(AR_INC));
  ControlUnitPC controlunitpc_1 (
    .R(R), .T1(T1), .T2(T2), .T3(T3), .T4(T4), .T5(T5), .T6(T6), .D4(D4), .D5(D5), .D6(D6), .D7(D7), .I(I),
    .DR(DR), .B1(B1), .B2(B2), .B3(B3), .B4(B4), .B8(B8), .B9(B9), .AC15(AC15), .AC(AC), .E(E), .FGI(FGI),
    .FGO(FGO), .PC_LD(PC_LD), .PC_CLR(PC_CLR), .PC_INC(PC_INC));
  ControlUnitDR controlunitdr_1 (.T4(T4), .T5(T5), .D0(D0), .D1(D1), .D2(D2), .D6(D6), .DR_LD(DR_LD), .DR_INC(DR_INC));
  ControlUnitAC controlunitac_1 (
    .I(I), .T3(T3), .T5(T5), .D0(D0), .D1(D1), .D2(D2), .D7(D7), .B5(B5), .B6(B6), .B7(B7), .B9(B9),
    .B11(B11), .AC_LD(AC_LD), .AC_CLR(AC_CLR), .AC_INC(AC_INC));
  ControlUnitALU controlunitalu_1 (
    .I(I), .T3(T3), .T5(T5), .D0(D0), .D7(D7), .B6(B6), .B7(B7), .B9(B9), .B11(B11), .D2(D2), .E(E),
    .CIN(ALU_CIN), .S0(ALU_S0), .S1(ALU_S1), .S2(ALU_S2), .S3(ALU_S3), .B(ALU_B));
  ControlUnitIR controlunitir_1 (.R(R), .T1(T1), .IR_LD(IR_LD));
  ControlUnitTR controlunittr_1 (.R(R), .T0(T0), .TR_LD(TR_LD));
  ControlUnitOUTR controlunitoutr_1 (.I(I), .T3(T3), .D7(D7), .B10(B10), .OUTR_LD(OUTR_LD));
  ControlUnitCommonBus controlunitcommonbus_1 (
    .R(R), .I(I), .T0(T0), .T1(T1), .T2(T2), .T3(T3), .T4(T4), .T5(T5), .T6(T6), .D0(D0), .D1(D1), .D2(D2),
    .D3(D3), .D4(D4), .D5(D5), .D6(D6), .D7(D7), .B10(B10), .CommonBus(CommonBus));
  ControlUnitCounter controlunitcounter_1 (
    .R(R), .T2(T2), .T3(T3), .T4(T4), .T5(T5), .T6(T6), .D0(D0), .D1(D1), .D2(D2), .D3(D3), .D4(D4), .D5(D5),
    .D6(D6), .D7(D7), .I(I), .SC_R(CounterR));
  ControlUnitR controlunitr_1 (.R(R), .T0(T0), .T1(T1), .T2(T2), .IEN(IEN), .FGI(FGI), .FGO(FGO), .R_TOGGLE(R_TOGGLE));
  ControlUnitIEN controlunitien_1 (
    .R(R), .I(I), .T2(T2), .T3(T3), .D7(D7), .B6(B6), .B7(B7), .IEN(IEN), .IEN_TOGGLE(IEN_TOGGLE));
  ControlUnitFGIO controlunitfgio_1 (.I(I), .T3(T3), .D7(D7), .B10(B10), .B11(B11), .FGI_R(FGI_R), .FGO_R(FGO_R));
  ControlUnitS controlunits_1 (.I(I), .T3(T3), .D7(D7), .B0(B0), .S_R(S_R));
  ControlUnitE controlunite_1 (
    .I(I), .T3(T3), .T5(T5), .D1(D1), .D7(D7), .B8(B8), .B10(B10), .E(E), .COUT(COUT), .B6(B6), .B7(B7),
    .E_TOGGLE(E_TOGGLE));
endmodule

module ControlUnitAR (
  input  R,
  input  I,
  input  T0,
  input  T2,
  input  T3,
  input  T4,
  input  D5,
  input  D7,
  output AR_LD,
  output AR_CLR,
  output AR_INC
);

  wire and_1_out, and_2_out, not_1_out, not_2_out, or_1_out;

  not not_1 (not_1_out, R);
  not not_2 (not_2_out, D7);
  or or_1 (or_1_out, T0, T2);
  and and_1 (and_1_out, or_1_out, not_1_out);
  and and_2 (and_2_out, I, T3, not_2_out);
  or or_2 (AR_LD, and_1_out, and_2_out);
  and and_3 (AR_CLR, R, T0);
  and and_4 (AR_INC, T4, D5);
endmodule

module ControlUnitPC (
  input  R,
  input  T1,
  input  T2,
  input  T3,
  input  T4,
  input  T5,
  input  T6,
  input  D4,
  input  D5,
  input  D6,
  input  D7,
  input  I,
  input  DR,
  input  B1,
  input  B2,
  input  B3,
  input  B4,
  input  B8,
  input  B9,
  input  AC15,
  input  AC,
  input  E,
  input  FGI,
  input  FGO,
  output PC_LD,
  output PC_CLR,
  output PC_INC
);

  wire and_1_out, and_2_out, and_3_out, and_4_out, and_5_out, and_6_out, and_7_out, and_8_out, and_9_out,
       and_10_out, and_11_out, and_12_out, and_13_out, and_14_out, and_15_out, and_16_out, not_1_out,
       not_2_out, not_3_out, not_4_out, not_5_out, not_6_out, or_1_out, or_2_out;

  not not_1 (not_1_out, R);
  and and_1 (and_1_out, D7, T3);
  not not_2 (not_2_out, I);
  not not_3 (not_3_out, DR);
  not not_4 (not_4_out, AC15);
  not not_5 (not_5_out, AC);
  not not_6 (not_6_out, E);
  and and_2 (and_2_out, D5, T5);
  and and_3 (and_3_out, B1, not_6_out);
  and and_4 (and_4_out, not_5_out, B2);
  and and_5 (and_5_out, B3, AC15);
  and and_6 (and_6_out, B4, not_4_out);
  and and_7 (and_7_out, FGO, B8);
  and and_8 (and_8_out, B9, FGI);
  and and_9 (and_9_out, D4, T4);
  and and_10 (and_10_out, not_1_out, T1);
  and and_11 (and_11_out, R, T2);
  and and_12 (and_12_out, not_3_out, D6, T6);
  and and_13 (and_13_out, not_2_out, and_1_out);
  or or_1 (or_1_out, and_3_out, and_4_out, and_5_out, and_6_out);
  or or_2 (or_2_out, and_7_out, and_8_out);
  and and_14 (and_14_out, and_1_out, I);
  and and_15 (and_15_out, and_13_out, or_1_out);
  and and_16 (and_16_out, and_14_out, or_2_out);
  or or_3 (PC_LD, and_2_out, and_9_out);
  and and_17 (PC_CLR, R, T1);
  or or_4 (PC_INC, and_10_out, and_11_out, and_12_out, and_15_out, and_16_out);
endmodule

module ControlUnitDR (
  input  T4,
  input  T5,
  input  D0,
  input  D1,
  input  D2,
  input  D6,
  output DR_LD,
  output DR_INC
);

  wire or_1_out;

  or or_1 (or_1_out, D0, D1, D2, D6);
  and and_1 (DR_LD, or_1_out, T4);
  and and_2 (DR_INC, T5, D6);
endmodule

module ControlUnitIR (
  input  R,
  input  T1,
  output IR_LD
);

  wire not_1_out;

  not not_1 (not_1_out, R);
  and and_1 (IR_LD, not_1_out, T1);
endmodule

module ControlUnitAC (
  input  I,
  input  T3,
  input  T5,
  input  D0,
  input  D1,
  input  D2,
  input  D7,
  input  B5,
  input  B6,
  input  B7,
  input  B9,
  input  B11,
  output AC_LD,
  output AC_CLR,
  output AC_INC
);

  wire and_1_out, and_2_out, and_3_out, and_4_out, and_5_out, and_6_out, not_1_out, or_1_out, or_2_out;

  and and_1 (and_1_out, D7, T3);
  not not_1 (not_1_out, I);
  or or_1 (or_1_out, D0, D1, D2);
  and and_2 (and_2_out, not_1_out, and_1_out);
  or or_2 (or_2_out, B6, B7, B9);
  and and_3 (and_3_out, and_1_out, I);
  and and_4 (and_4_out, or_1_out, T5);
  and and_5 (and_5_out, and_2_out, or_2_out);
  and and_6 (and_6_out, and_3_out, B11);
  or or_3 (AC_LD, and_4_out, and_5_out, and_6_out);
  and and_7 (AC_CLR, and_2_out, B11);
  and and_8 (AC_INC, B5, and_2_out);
endmodule

module ControlUnitOUTR (
  input  I,
  input  T3,
  input  D7,
  input  B10,
  output OUTR_LD
);

  and and_1 (OUTR_LD, I, T3, D7, B10);
endmodule

module ControlUnitTR (
  input  R,
  input  T0,
  output TR_LD
);

  and and_1 (TR_LD, R, T0);
endmodule

module ControlUnitMemory (
  input  R,
  input  I,
  input  T1,
  input  T3,
  input  T4,
  input  T6,
  input  D0,
  input  D1,
  input  D2,
  input  D3,
  input  D5,
  input  D6,
  input  D7,
  output M_WRT,
  output M_RD
);

  wire and_1_out, and_2_out, and_3_out, and_4_out, and_5_out, and_6_out, not_1_out, not_2_out, or_1_out,
       or_2_out;

  not not_1 (not_1_out, D7);
  not not_2 (not_2_out, R);
  or or_1 (or_1_out, D3, D5);
  or or_2 (or_2_out, D0, D1, D2, D6);
  and and_1 (and_1_out, R, T1);
  and and_2 (and_2_out, T4, or_1_out);
  and and_3 (and_3_out, D6, T6);
  and and_4 (and_4_out, T1, not_2_out);
  and and_5 (and_5_out, not_1_out, T3, I);
  and and_6 (and_6_out, T4, or_2_out);
  or or_3 (M_WRT, and_1_out, and_2_out, and_3_out);
  or or_4 (M_RD, and_4_out, and_5_out, and_6_out);
endmodule

module ControlUnitCommonBus (
  input  R,
  input  I,
  input  T0,
  input  T1,
  input  T2,
  input  T3,
  input  T4,
  input  T5,
  input  T6,
  input  D0,
  input  D1,
  input  D2,
  input  D3,
  input  D4,
  input  D5,
  input  D6,
  input  D7,
  input  B10,
  output [2:0] CommonBus
);

  wire and_1_out, and_2_out, and_3_out, and_4_out, and_5_out, and_6_out, and_7_out, and_8_out, and_9_out,
       and_10_out, and_11_out, and_12_out, not_1_out, not_2_out, or_1_out, or_2_out, or_3_out, or_4_out,
       or_5_out, or_6_out;

  not not_1 (not_1_out, R);
  not not_2 (not_2_out, D7);
  or or_1 (or_1_out, D0, D1, D2, D6);
  and and_1 (and_1_out, T4, or_1_out);
  and and_2 (and_2_out, I, T3, not_2_out);
  and and_3 (and_3_out, T1, not_1_out);
  and and_4 (and_4_out, T4, D3);
  and and_5 (and_5_out, B10, T3, I, D7);
  and and_6 (and_6_out, T5, D2);
  and and_7 (and_7_out, D6, T6);
  and and_8 (and_8_out, T4, D5);
  and and_9 (and_9_out, T4, D4);
  and and_10 (and_10_out, T5, D5);
  or or_2 (or_2_out, and_1_out, and_2_out, and_3_out);
  and and_11 (and_11_out, R, T1);
  and and_12 (and_12_out, T2, not_1_out);
  or or_3 (or_3_out, and_4_out, and_5_out);
  or or_4 (or_4_out, and_6_out, and_7_out);
  or or_5 (or_5_out, and_8_out, T0);
  or or_6 (or_6_out, and_9_out, and_10_out);
  Encoder3Bit encoder3bit_1 (
    .I7(or_2_out), .I6(and_11_out), .I5(and_12_out), .I4(or_3_out), .I3(or_4_out), .I2(or_5_out),
    .I1(or_6_out), .S0(CommonBus[0]), .S1(CommonBus[1]), .S2(CommonBus[2]));  // open: I0
endmodule

module ControlUnitR (
  input  R,
  input  T0,
  input  T1,
  input  T2,
  input  IEN,
  input  FGI,
  input  FGO,
  output R_TOGGLE
);

  wire and_1_out, and_2_out, not_1_out, not_2_out, not_3_out, not_4_out, or_1_out;

  not not_1 (not_1_out, R);
  not not_2 (not_2_out, T0);
  not not_3 (not_3_out, T1);
  not not_4 (not_4_out, T2);
  or or_1 (or_1_out, FGI, FGO);
  and and_1 (and_1_out, R, T2);
  and and_2 (and_2_out, not_2_out, not_3_out, not_4_out, IEN, or_1_out, not_1_out);
  or or_2 (R_TOGGLE, and_1_out, and_2_out);
endmodule

module ControlUnitIEN (
  input  R,
  input  I,
  input  T2,
  input  T3,
  input  D7,
  input  B6,
  input  B7,
  input  IEN,
  output IEN_TOGGLE
);

  wire and_1_out, and_2_out, and_3_out, and_4_out, and_5_out, not_1_out, or_1_out;

  not not_1 (not_1_out, IEN);
  and and_1 (and_1_out, B6, IEN);
  and and_2 (and_2_out, not_1_out, B7);
  and and_3 (and_3_out, D7, T3, I);
  or or_1 (or_1_out, and_1_out, and_2_out);
  and and_4 (and_4_out, R, T2, IEN);
  and and_5 (and_5_out, and_3_out, or_1_out);
  or or_2 (IEN_TOGGLE, and_4_out, and_5_out);
endmodule

module ControlUnitFGIO (
  input  I,
  input  T3,
  input  D7,
  input  B10,
  input  B11,
  output FGI_R,
  output FGO_R
);

  wire and_1_out;

  and and_1 (and_1_out, I, D7, T3);
  and and_2 (FGI_R, and_1_out, B11);
  and and_3 (FGO_R, and_1_out, B10);
endmodule

module ControlUnitCounter (
  input  R,
  input  T2,
  input  T3,
  input  T4,
  input  T5,
  input  T6,
  input  D0,
  input  D1,
  input  D2,
  input  D3,
  input  D4,
  input  D5,
  input  D6,
  input  D7,
  input  I,
  output SC_R
);

  wire and_1_out, and_2_out, and_3_out, and_4_out, and_5_out, and_6_out, not_1_out, or_1_out, or_2_out,
       or_3_out;

  not not_1 (not_1_out, I);
  or or_1 (or_1_out, D0, D1, D2, D5);
  or or_2 (or_2_out, D4, D3);
  and and_1 (and_1_out, T6, D6);
  and and_2 (and_2_out, D7, T3);
  or or_3 (or_3_out, I, not_1_out);
  and and_3 (and_3_out, R, T2);
  and and_4 (and_4_out, T5, or_1_out);
  and and_5 (and_5_out, or_2_out, T4);
  and and_6 (and_6_out, and_2_out, or_3_out);
  or or_4 (SC_R, and_3_out, and_4_out, and_5_out, and_1_out, and_6_out);
endmodule

module ControlUnitALU (
  input  I,
  input  T3,
  input  T5,
  input  D0,
  input  D7,
  input  B6,
  input  B7,
  input  B9,
  input  B11,
  input  D2,
  input  E,
  output CIN,
  output S0,
  output S1,
  output S2,
  output S3,
  output B
);

  wire and_1_out, and_2_out, and_3_out, and_4_out, and_5_out, and_6_out, and_7_out, and_8_out, and_9_out,
       and_10_out, and_11_out, and_12_out, not_1_out, or_1_out, or_2_out, or_3_out, or_4_out;

  not not_1 (not_1_out, I);
  and and_1 (and_1_out, T3, D7);
  or or_1 (or_1_out, B6, B7);
  and and_2 (and_2_out, not_1_out, and_1_out);
  and and_3 (and_3_out, I, B11);
  and and_4 (and_4_out, not_1_out, or_1_out);
  or or_2 (or_2_out, B9, B6);
  or or_3 (or_3_out, and_3_out, and_4_out);
  or or_4 (or_4_out, D0, D2);
  and and_5 (and_5_out, I, and_1_out);
  and and_6 (and_6_out, E, S3);
  and and_7 (and_7_out, and_2_out, B9);
  and and_8 (and_8_out, and_2_out, or_2_out);
  and and_9 (and_9_out, and_1_out, or_3_out);
  and and_10 (and_10_out, D2, T5);
  and and_11 (and_11_out, T5, or_4_out);
  and and_12 (and_12_out, and_2_out, B9);
  and and_13 (S3, and_2_out, or_1_out);
  and and_14 (B, and_5_out, B11);
  or or_5 (CIN, and_6_out, and_7_out);
  or or_6 (S0, and_8_out, and_10_out);
  or or_7 (S1, and_9_out, and_10_out);
  or or_8 (S2, and_11_out, and_12_out, and_5_out);
endmodule

module ControlUnitS (
  input  I,
  input  T3,
  input  D7,
  input  B0,
  output S_R
);

  wire not_1_out;

  not not_1 (not_1_out, I);
  and and_1 (S_R, not_1_out, T3, D7, B0);
endmodule

module ControlUnitE (
  input  I,
  input  T3,
  input  T5,
  input  D1,
  input  D7,
  input  B8,
  input  B10,
  input  E,
  input  COUT,
  input  B6,
  input  B7,
  output E_TOGGLE
);

  wire and_1_out, and_2_out, and_3_out, and_4_out, and_5_out, not_1_out, or_1_out, or_2_out, xor_1_out;

  not not_1 (not_1_out, I);
  or or_1 (or_1_out, B6, B7);
  and and_1 (and_1_out, B10, E);
  xor xor_1 (xor_1_out, E, COUT);
  and and_2 (and_2_out, D7, not_1_out, T3);
  or or_2 (or_2_out, B8, and_1_out);
  and and_3 (and_3_out, and_2_out, or_2_out);
  and and_4 (and_4_out, T5, xor_1_out, D1);
  and and_5 (and_5_out, xor_1_out, or_1_out, and_2_out);
  or or_3 (E_TOGGLE, and_3_out, and_4_out, and_5_out);
endmodule

module FullAdder4Bit (
  input  [3:0] A,
  input  [3:0] B,
  input  CIN,
  output COUT,
  output [3:0] S
);

  wire fulladder1bit_1_cout, fulladder1bit_2_cout, fulladder1bit_3_cout;

  FullAdder1Bit fulladder1bit_1 (.A(A[0]), .B(B[0]), .CIN(CIN), .S(S[0]), .COUT(fulladder1bit_1_cout));
  FullAdder1Bit fulladder1bit_2 (.A(A[1]), .B(B[1]), .CIN(fulladder1bit_1_cout), .S(S[1]), .COUT(fulladder1bit_2_cout));
  FullAdder1Bit fulladder1bit_3 (.A(A[2]), .B(B[2]), .CIN(fulladder1bit_2_cout), .S(S[2]), .COUT(fulladder1bit_3_cout));
  FullAdder1Bit fulladder1bit_4 (.A(A[3]), .B(B[3]), .CIN(fulladder1bit_3_cout), .S(S[3]), .COUT(COUT));
endmodule

module FullAdder12Bit (
  input  [11:0] A,
  input  [11:0] B,
  input  CIN,
  output COUT,
  output [11:0] S
);

  wire fulladder1bit_1_cout, fulladder1bit_2_cout, fulladder1bit_3_cout, fulladder1bit_4_cout,
       fulladder1bit_5_cout, fulladder1bit_6_cout, fulladder1bit_7_cout, fulladder1bit_8_cout,
       fulladder1bit_9_cout, fulladder1bit_10_cout, fulladder1bit_11_cout;

  FullAdder1Bit fulladder1bit_1 (.A(A[0]), .B(B[0]), .CIN(CIN), .S(S[0]), .COUT(fulladder1bit_1_cout));
  FullAdder1Bit fulladder1bit_2 (.A(A[1]), .B(B[1]), .CIN(fulladder1bit_1_cout), .S(S[1]), .COUT(fulladder1bit_2_cout));
  FullAdder1Bit fulladder1bit_3 (.A(A[2]), .B(B[2]), .CIN(fulladder1bit_2_cout), .S(S[2]), .COUT(fulladder1bit_3_cout));
  FullAdder1Bit fulladder1bit_4 (.A(A[3]), .B(B[3]), .CIN(fulladder1bit_3_cout), .S(S[3]), .COUT(fulladder1bit_4_cout));
  FullAdder1Bit fulladder1bit_5 (.A(A[4]), .B(B[4]), .CIN(fulladder1bit_4_cout), .S(S[4]), .COUT(fulladder1bit_5_cout));
  FullAdder1Bit fulladder1bit_6 (.A(A[5]), .B(B[5]), .CIN(fulladder1bit_5_cout), .S(S[5]), .COUT(fulladder1bit_6_cout));
  FullAdder1Bit fulladder1bit_7 (.A(A[6]), .B(B[6]), .CIN(fulladder1bit_6_cout), .S(S[6]), .COUT(fulladder1bit_7_cout));
  FullAdder1Bit fulladder1bit_8 (.A(A[7]), .B(B[7]), .CIN(fulladder1bit_7_cout), .S(S[7]), .COUT(fulladder1bit_8_cout));
  FullAdder1Bit fulladder1bit_9 (.A(A[8]), .B(B[8]), .CIN(fulladder1bit_8_cout), .S(S[8]), .COUT(fulladder1bit_9_cout));
  FullAdder1Bit fulladder1bit_10 (
    .A(A[9]), .B(B[9]), .CIN(fulladder1bit_9_cout), .S(S[9]), .COUT(fulladder1bit_10_cout));
  FullAdder1Bit fulladder1bit_11 (
    .A(A[10]), .B(B[10]), .CIN(fulladder1bit_10_cout), .S(S[10]), .COUT(fulladder1bit_11_cout));
  FullAdder1Bit fulladder1bit_12 (.A(A[11]), .B(B[11]), .CIN(fulladder1bit_11_cout), .S(S[11]), .COUT(COUT));
endmodule

module Register4Bit (
  input  [3:0] I,
  input  LD,
  input  CLK,
  output [3:0] O
);

  wire [3:0] multiplexer_1_out;

  Multiplexer #(.width(4)) multiplexer_1 (.in0(O), .in1(I), .out(multiplexer_1_out), .sel(LD));
  D_Flip_Flop d_ff_1 (.D(multiplexer_1_out[0]), .clk(CLK), .Q(O[0]));  // open: Qn, preset, reset
  D_Flip_Flop d_ff_2 (.D(multiplexer_1_out[1]), .clk(CLK), .Q(O[1]));  // open: Qn, preset, reset
  D_Flip_Flop d_ff_3 (.D(multiplexer_1_out[2]), .clk(CLK), .Q(O[2]));  // open: Qn, preset, reset
  D_Flip_Flop d_ff_4 (.D(multiplexer_1_out[3]), .clk(CLK), .Q(O[3]));  // open: Qn, preset, reset
endmodule

module Encoder3Bit (
  input  I7,
  input  I6,
  input  I5,
  input  I4,
  input  I3,
  input  I2,
  input  I1,
  input  I0,
  output S0,
  output S1,
  output S2
);

  or or_1 (S0, I1, I3, I5, I7);
  or or_2 (S1, I2, I3, I6, I7);
  or or_3 (S2, I4, I5, I6, I7);
endmodule
